// Digital circuit MMU.dig as structural Verilog
module MMU (
  input  [7:0] DATA,
  input  [15:0] ADDRESS,
  input  MREAD,
  input  MWRITE,
  input  [7:0] IN_0,
  input  [7:0] IN_1,
  input  [7:0] IN_2,
  input  [7:0] IN_3,
  input  [7:0] IN_4,
  input  [7:0] IN_5,
  input  [7:0] IN_6,
  input  [7:0] IN_7,
  output [7:0] LED_R0,
  output [7:0] LED_R1,
  output [7:0] LED_R2,
  output [7:0] LED_R3,
  output [7:0] LED_R4,
  output [7:0] LED_R5,
  output [7:0] LED_R6,
  output [7:0] LED_R7
);

  wire _74138_1_pin13, _74138_1_pin14, _74138_1_pin15, _74138_2_pin14, _74138_2_pin15, _74138_3_pin7,
       _74138_3_pin9, _74138_3_pin10, _74138_3_pin11, _74138_3_pin12, _74138_3_pin13, _74138_3_pin14,
       _74138_3_pin15, _74138_4_pin7, _74138_4_pin9, _74138_4_pin10, _74138_4_pin11, _74138_4_pin12,
       _74138_4_pin13, _74138_4_pin14, _74138_4_pin15, and_1_out, nor_1_out, not_1_out, not_2_out;

  _74138 _74138_1 (
    .pin1(ADDRESS[13]), .pin2(ADDRESS[14]), .pin3(ADDRESS[15]), .pin4(1'b0), .pin5(1'b0), .pin6(1'b1),
    .pin8(1'b0), .pin13(_74138_1_pin13), .pin14(_74138_1_pin14), .pin15(_74138_1_pin15), .pin16(1'b1));  // open: pin7, pin9, pin10, pin11, pin12
  and and_1 (and_1_out, _74138_1_pin15, _74138_1_pin14);
  RAMSinglePortSel #(.AddrBits(15), .Bits(8)) ramsingleportsel_1 (
    .A(ADDRESS[14:0]), .CS(ADDRESS[15]), .WE(not_1_out), .OE(not_2_out), .D(DATA));
  not not_1 (not_1_out, MWRITE);
  not not_2 (not_2_out, MREAD);
  ROM #(.AddrBits(14), .isProgramMemory("true"), .Bits(8)) rom_1 (.A(ADDRESS[13:0]), .sel(nor_1_out), .D(DATA));
  nor nor_1 (nor_1_out, MREAD, and_1_out);
  _74138 _74138_2 (
    .pin1(ADDRESS[10]), .pin2(ADDRESS[11]), .pin3(ADDRESS[12]), .pin4(_74138_1_pin13), .pin5(1'b0),
    .pin6(1'b1), .pin8(1'b0), .pin14(_74138_2_pin14), .pin15(_74138_2_pin15), .pin16(1'b1));  // open: pin7, pin9, pin10, pin11, pin12, pin13
  _74138 _74138_3 (
    .pin1(ADDRESS[0]), .pin2(ADDRESS[1]), .pin3(ADDRESS[2]), .pin4(_74138_2_pin15), .pin5(1'b0), .pin6(1'b1),
    .pin7(_74138_3_pin7), .pin8(1'b0), .pin9(_74138_3_pin9), .pin10(_74138_3_pin10), .pin11(_74138_3_pin11),
    .pin12(_74138_3_pin12), .pin13(_74138_3_pin13), .pin14(_74138_3_pin14), .pin15(_74138_3_pin15),
    .pin16(1'b1));
  _74138 _74138_4 (
    .pin1(ADDRESS[0]), .pin2(ADDRESS[1]), .pin3(ADDRESS[2]), .pin4(_74138_2_pin14), .pin5(MREAD),
    .pin6(1'b1), .pin7(_74138_4_pin7), .pin8(1'b0), .pin9(_74138_4_pin9), .pin10(_74138_4_pin10),
    .pin11(_74138_4_pin11), .pin12(_74138_4_pin12), .pin13(_74138_4_pin13), .pin14(_74138_4_pin14),
    .pin15(_74138_4_pin15), .pin16(1'b1));
  Register #(.Bits(8)) register_1 (.D(DATA), .C(~MWRITE), .en(~_74138_3_pin15), .Q(LED_R0));
  Register #(.Bits(8)) register_2 (.D(DATA), .C(~MWRITE), .en(~_74138_3_pin14), .Q(LED_R1));
  Register #(.Bits(8)) register_3 (.D(DATA), .C(~MWRITE), .en(~_74138_3_pin13), .Q(LED_R2));
  Register #(.Bits(8)) register_4 (.D(DATA), .C(~MWRITE), .en(~_74138_3_pin12), .Q(LED_R3));
  Register #(.Bits(8)) register_5 (.D(DATA), .C(~MWRITE), .en(~_74138_3_pin11), .Q(LED_R4));
  Register #(.Bits(8)) register_6 (.D(DATA), .C(~MWRITE), .en(~_74138_3_pin10), .Q(LED_R5));
  Register #(.Bits(8)) register_7 (.D(DATA), .C(~MWRITE), .en(~_74138_3_pin9), .Q(LED_R6));
  Register #(.Bits(8)) register_8 (.D(DATA), .C(~MWRITE), .en(~_74138_3_pin7), .Q(LED_R7));
  assign DATA = ~_74138_4_pin15 ? IN_0 : 8'bz;  // DriverInvSel driverinvsel_1
  assign DATA = ~_74138_4_pin14 ? IN_1 : 8'bz;  // DriverInvSel driverinvsel_2
  assign DATA = ~_74138_4_pin13 ? IN_2 : 8'bz;  // DriverInvSel driverinvsel_3
  assign DATA = ~_74138_4_pin12 ? IN_3 : 8'bz;  // DriverInvSel driverinvsel_4
  assign DATA = ~_74138_4_pin11 ? IN_4 : 8'bz;  // DriverInvSel driverinvsel_5
  assign DATA = ~_74138_4_pin10 ? IN_5 : 8'bz;  // DriverInvSel driverinvsel_6
  assign DATA = ~_74138_4_pin9 ? IN_6 : 8'bz;  // DriverInvSel driverinvsel_7
  assign DATA = ~_74138_4_pin7 ? IN_7 : 8'bz;  // DriverInvSel driverinvsel_8

  // Notes on the sheet:
  //   DATA: pin 1
  //   ADDRESS: pin 4
  //   MREAD: pin 2, default 1
  //   MWRITE: pin 3, default 1
  //   LED_R0: pin 32
  //   LED_R1: pin 31
  //   LED_R2: pin 30
  //   LED_R3: pin 29
  //   LED_R4: pin 28
  //   LED_R5: pin 27
  //   LED_R6: pin 26
  //   LED_R7: pin 25
  //   IN_0: pin 24
  //   IN_1: pin 23
  //   IN_2: pin 22
  //   IN_3: pin 21
  //   IN_4: pin 20
  //   IN_5: pin 19
  //   IN_6: pin 18
  //   IN_7: pin 17
  //   rom_1 loads leds.s.hex
endmodule
