// Digital circuit cpu.dig as structural Verilog
module cpu (
  input  clk
);

  wire and_1_out, and_2_out, decode_1_p1, decode_1_p4, decode_1_p5, decode_1_p6, decode_1_p7, decode_1_p8,
       decode_1_p9, decode_1_p10, decode_1_p11, decode_1_p12, decode_1_p13, decode_1_p14, decode_1_p15,
       decode_1_p16, decode_1_p17, decode_1_p18, decode_1_p19, decode_1_p20, decode_1_p21, decode_1_p22,
       decode_1_p23, decode_1_p24, decode_1_p25, decode_1_p26, decode_1_p27, decode_1_p28, delay_1_out,
       delay_2_out, delay_3_out, mmu_1_dbg_int_enabled, mmu_1_term_sel, not_1_out, not_2_out, not_3_out,
       not_4_out, not_5_out, or_1_out, or_2_out, or_3_out, Reset_out, telnet_1_av, undriven, undriven_2,
       undriven_3, undriven_4, undriven_5, undriven_6, undriven_7, undriven_8, undriven_9, undriven_10,
       undriven_11, undriven_12, undriven_13, undriven_14, undriven_15, undriven_16, undriven_19,
       undriven_21, undriven_22, undriven_23, undriven_24, undriven_25;
  wire [3:0] _16_bit_reg_cnt_1_address_2, _16_bit_reg_cnt_1_address_3, _16_bit_reg_cnt_2_dbg_2,
       _16_bit_reg_cnt_2_dbg_3, _16_bit_reg_cnt_3_dbg_2, _16_bit_reg_cnt_3_dbg_3, alu_board_1_dbg_a,
       alu_board_1_dbg_a_2, alu_board_1_dbg_b, alu_board_1_dbg_b_2, decode_1_p2, decode_1_p2_2, undriven_17;
  wire [4:0] undriven_20;
  wire [7:0] _16_bit_reg_cnt_1_address, _16_bit_reg_cnt_2_dbg, _16_bit_reg_cnt_3_dbg, button_1_out,
       counter_1_out, counter_2_out, dipswitch_1_out, dipswitch_3_out, mmu_1_led_r0, mmu_1_led_r1,
       mmu_1_led_r2, mmu_1_led_r3, mmu_1_led_r4, mmu_1_led_r5, mmu_1_led_r6, mmu_1_led_r7;
  wire [7:4] undriven_18;
  wire [15:0] _16_bit_reg_cnt_1_dbg;

  Seven_Seg_Hex seven_seg_hex_1 (.d(undriven_18), .dp(1'b0));
  not not_1 (not_1_out, undriven);
  and and_1 (and_1_out, clk, not_1_out);
  Seven_Seg_Hex seven_seg_hex_2 (.d(undriven_17), .dp(1'b0));
  Seven_Seg_Hex seven_seg_hex_3 (.d(decode_1_p2_2), .dp(1'b0));
  Seven_Seg_Hex seven_seg_hex_4 (.d(decode_1_p2), .dp(1'b0));
  // decode decode_1: pin names not known; wires that end beside it: decode_1_p1, {decode_1_p2_2, decode_1_p2}, and_1_out, decode_1_p4, decode_1_p5, decode_1_p6, decode_1_p7, decode_1_p8, decode_1_p9, decode_1_p10, decode_1_p11, decode_1_p12, decode_1_p13, decode_1_p14, decode_1_p15, decode_1_p16, decode_1_p17, decode_1_p18, decode_1_p19, decode_1_p20, decode_1_p21, decode_1_p22, decode_1_p23, decode_1_p24, decode_1_p25, decode_1_p26, decode_1_p27, decode_1_p28
  Seven_Seg_Hex seven_seg_hex_5 (.d(_16_bit_reg_cnt_1_address_3), .dp(1'b0));
  Seven_Seg_Hex seven_seg_hex_6 (.d(_16_bit_reg_cnt_1_address_2), .dp(1'b0));
  Seven_Seg_Hex seven_seg_hex_7 (.d(_16_bit_reg_cnt_1_address[7:4]), .dp(1'b0));
  Seven_Seg_Hex seven_seg_hex_8 (.d(_16_bit_reg_cnt_1_address[3:0]), .dp(1'b0));
  _16_bit_reg_cnt _16_bit_reg_cnt_1 (
    .LOW_D(decode_1_p11), .HIGH_D(decode_1_p10), .OUT_A(decode_1_p15), .LOW_LD(decode_1_p22),
    .HIGH_LD(decode_1_p21), .INC(decode_1_p27), .DEC(decode_1_p26), .RST(undriven_21),
    .DATA({decode_1_p2_2, decode_1_p2}), .DATA_OUT({decode_1_p2_2, decode_1_p2}),
    .Address({_16_bit_reg_cnt_1_address_3, _16_bit_reg_cnt_1_address_2, _16_bit_reg_cnt_1_address}),
    .DBG(_16_bit_reg_cnt_1_dbg));
  alu_board alu_board_1 (
    .DATA({decode_1_p2_2, decode_1_p2}), .A_i(undriven_2), .A_o(undriven_3), .ALU_latch(undriven_22),
    .B_i(decode_1_p20), .B_o(decode_1_p9), .ALU_OP(undriven_20), .ALU_d(decode_1_p16), .ALUF_d(decode_1_p18),
    .F_o(decode_1_p19), .F_i(decode_1_p28), .DATA_OUT({decode_1_p2_2, decode_1_p2}), .C(decode_1_p4),
    .Z(decode_1_p5), .SF(decode_1_p6), .OF(decode_1_p7), .DBG_A({alu_board_1_dbg_a_2, alu_board_1_dbg_a}),
    .DBG_B({alu_board_1_dbg_b_2, alu_board_1_dbg_b}));
  mar mar_1 (
    .LOW_D(decode_1_p13), .HIGH_D(decode_1_p12), .MF_A(decode_1_p17), .LOW_LD(decode_1_p24),
    .HIGH_LD(decode_1_p23), .INC(1'b1), .DEC(1'b1), .RST(decode_1_p1), .DATA({decode_1_p2_2, decode_1_p2}),
    .OFF_i(decode_1_p25), .OFF_o(decode_1_p14), .off_im(undriven_19), .imm(undriven_20),
    .DATA_OUT({decode_1_p2_2, decode_1_p2}),
    .Address({_16_bit_reg_cnt_1_address_3, _16_bit_reg_cnt_1_address_2, _16_bit_reg_cnt_1_address}));
  _16_bit_reg_cnt _16_bit_reg_cnt_2 (
    .LOW_D(undriven_5), .HIGH_D(undriven_4), .OUT_A(undriven_15), .LOW_LD(undriven_7), .HIGH_LD(undriven_6),
    .INC(undriven_14), .DEC(1'b1), .RST(decode_1_p1), .DATA({decode_1_p2_2, decode_1_p2}),
    .DATA_OUT({decode_1_p2_2, decode_1_p2}),
    .Address({_16_bit_reg_cnt_1_address_3, _16_bit_reg_cnt_1_address_2, _16_bit_reg_cnt_1_address}),
    .DBG({_16_bit_reg_cnt_2_dbg_3, _16_bit_reg_cnt_2_dbg_2, _16_bit_reg_cnt_2_dbg}));
  _16_bit_reg_cnt _16_bit_reg_cnt_3 (
    .LOW_D(undriven_11), .HIGH_D(undriven_10), .OUT_A(undriven_9), .LOW_LD(undriven_13),
    .HIGH_LD(undriven_12), .INC(undriven_8), .DEC(1'b1), .RST(decode_1_p1),
    .DATA({decode_1_p2_2, decode_1_p2}), .DATA_OUT({decode_1_p2_2, decode_1_p2}),
    .Address({_16_bit_reg_cnt_1_address_3, _16_bit_reg_cnt_1_address_2, _16_bit_reg_cnt_1_address}),
    .DBG({_16_bit_reg_cnt_3_dbg_3, _16_bit_reg_cnt_3_dbg_2, _16_bit_reg_cnt_3_dbg}));
  RS_FF_AS rs_ff_as_1 (.S(Reset_out), .R(1'b0), .nQ(decode_1_p1));  // open: Q
  Button Reset (.out(Reset_out));
  Seven_Seg_Hex seven_seg_hex_9 (.d(alu_board_1_dbg_a_2), .dp(1'b0));
  Seven_Seg_Hex seven_seg_hex_10 (.d(_16_bit_reg_cnt_2_dbg_3), .dp(1'b0));
  Seven_Seg_Hex seven_seg_hex_11 (.d(_16_bit_reg_cnt_3_dbg_3), .dp(1'b0));
  LED led_1 (.in(mmu_1_dbg_int_enabled));
  Seven_Seg_Hex seven_seg_hex_12 (.d(alu_board_1_dbg_a), .dp(1'b0));
  Seven_Seg_Hex seven_seg_hex_13 (.d(_16_bit_reg_cnt_2_dbg_2), .dp(1'b0));
  Seven_Seg_Hex seven_seg_hex_14 (.d(_16_bit_reg_cnt_3_dbg_2), .dp(1'b0));
  MMU mmu_1 (
    .DATA({decode_1_p2_2, decode_1_p2}),
    .ADDRESS({_16_bit_reg_cnt_1_address_3, _16_bit_reg_cnt_1_address_2, _16_bit_reg_cnt_1_address}),
    .MREAD(undriven_24), .MWRITE(undriven_23), .LED_R0(mmu_1_led_r0), .LED_R1(mmu_1_led_r1),
    .LED_R2(mmu_1_led_r2), .LED_R3(mmu_1_led_r3), .LED_R4(mmu_1_led_r4), .LED_R5(mmu_1_led_r5),
    .LED_R6(mmu_1_led_r6), .LED_R7(mmu_1_led_r7), .IN_0(button_1_out), .IN_1(dipswitch_1_out),
    .IN_2(dipswitch_3_out), .IN_3({8{1'b0}}), .IN_4({8{1'b0}}), .IN_5({8{1'b0}}), .IN_6({8{1'b0}}),
    .IN_7({8{1'b0}}), .INT_0_EDGE(and_2_out), .INT_1_EDGE(button_1_out[1]), .INT_2_EDGE(button_1_out[2]),
    .INT_3_LEVEL(telnet_1_av), .P0(undriven_22), .RST(decode_1_p1), .IRQ(decode_1_p8), .iv_o(undriven_16),
    .ei(undriven_25), .TERM_SEL(mmu_1_term_sel), .DBG_int_enabled(mmu_1_dbg_int_enabled));
  or or_1 (or_1_out, mmu_1_term_sel, undriven_23);
  or or_2 (or_2_out, mmu_1_term_sel, undriven_24);
  Seven_Seg_Hex seven_seg_hex_15 (.d(alu_board_1_dbg_b_2), .dp(1'b0));
  Seven_Seg_Hex seven_seg_hex_16 (.d(_16_bit_reg_cnt_2_dbg[7:4]), .dp(1'b0));
  Seven_Seg_Hex seven_seg_hex_17 (.d(_16_bit_reg_cnt_3_dbg[7:4]), .dp(1'b0));
  Seven_Seg_Hex seven_seg_hex_18 (.d(alu_board_1_dbg_b), .dp(1'b0));
  Seven_Seg_Hex seven_seg_hex_19 (.d(_16_bit_reg_cnt_2_dbg[3:0]), .dp(1'b0));
  Seven_Seg_Hex seven_seg_hex_20 (.d(_16_bit_reg_cnt_3_dbg[3:0]), .dp(1'b0));
  not not_2 (not_2_out, or_1_out);
  not not_3 (not_3_out, or_2_out);
  Seven_Seg_Hex seven_seg_hex_21 (.d(_16_bit_reg_cnt_1_dbg[15:12]), .dp(1'b0));
  or or_3 (or_3_out, not_2_out, not_3_out);
  Seven_Seg_Hex seven_seg_hex_22 (.d(_16_bit_reg_cnt_1_dbg[11:8]), .dp(1'b0));
  Seven_Seg_Hex seven_seg_hex_23 (.d(_16_bit_reg_cnt_1_dbg[7:4]), .dp(1'b0));
  not not_4 (not_4_out, or_3_out);
  Button button_1 (.out(button_1_out[7]));
  Button button_2 (.out(button_1_out[6]));
  DipSwitch dipswitch_1 (.out(dipswitch_1_out[7]));
  DipSwitch dipswitch_2 (.out(dipswitch_1_out[6]));
  DipSwitch dipswitch_3 (.out(dipswitch_3_out[7]));
  DipSwitch dipswitch_4 (.out(dipswitch_3_out[6]));
  Seven_Seg_Hex seven_seg_hex_24 (.d(_16_bit_reg_cnt_1_dbg[3:0]), .dp(1'b0));
  Delay #(.delayTime(5)) delay_1 (.in(not_2_out), .out(delay_1_out));
  Delay #(.delayTime(5)) delay_2 (.in(not_3_out), .out(delay_2_out));
  LightBulb lightbulb_1 (.A(1'b0), .B(mmu_1_led_r0[7]));
  LightBulb lightbulb_2 (.A(1'b0), .B(mmu_1_led_r1[7]));
  LightBulb lightbulb_3 (.A(1'b0), .B(mmu_1_led_r2[7]));
  LightBulb lightbulb_4 (.A(1'b0), .B(mmu_1_led_r3[7]));
  LightBulb lightbulb_5 (.A(1'b0), .B(mmu_1_led_r4[7]));
  LightBulb lightbulb_6 (.A(1'b0), .B(mmu_1_led_r5[7]));
  LightBulb lightbulb_7 (.A(1'b0), .B(mmu_1_led_r6[7]));
  LightBulb lightbulb_8 (.A(1'b0), .B(mmu_1_led_r7[7]));
  Button button_3 (.out(button_1_out[5]));
  Button button_4 (.out(button_1_out[4]));
  DipSwitch dipswitch_5 (.out(dipswitch_1_out[5]));
  DipSwitch dipswitch_6 (.out(dipswitch_1_out[4]));
  DipSwitch dipswitch_7 (.out(dipswitch_3_out[5]));
  DipSwitch dipswitch_8 (.out(dipswitch_3_out[4]));
  LightBulb lightbulb_9 (.A(1'b0), .B(mmu_1_led_r0[6]));
  LightBulb lightbulb_10 (.A(1'b0), .B(mmu_1_led_r0[5]));
  LightBulb lightbulb_11 (.A(1'b0), .B(mmu_1_led_r1[6]));
  LightBulb lightbulb_12 (.A(1'b0), .B(mmu_1_led_r1[5]));
  LightBulb lightbulb_13 (.A(1'b0), .B(mmu_1_led_r2[6]));
  LightBulb lightbulb_14 (.A(1'b0), .B(mmu_1_led_r2[5]));
  LightBulb lightbulb_15 (.A(1'b0), .B(mmu_1_led_r3[6]));
  LightBulb lightbulb_16 (.A(1'b0), .B(mmu_1_led_r3[5]));
  LightBulb lightbulb_17 (.A(1'b0), .B(mmu_1_led_r4[6]));
  LightBulb lightbulb_18 (.A(1'b0), .B(mmu_1_led_r4[5]));
  LightBulb lightbulb_19 (.A(1'b0), .B(mmu_1_led_r5[6]));
  LightBulb lightbulb_20 (.A(1'b0), .B(mmu_1_led_r5[5]));
  LightBulb lightbulb_21 (.A(1'b0), .B(mmu_1_led_r6[6]));
  LightBulb lightbulb_22 (.A(1'b0), .B(mmu_1_led_r6[5]));
  LightBulb lightbulb_23 (.A(1'b0), .B(mmu_1_led_r7[6]));
  LightBulb lightbulb_24 (.A(1'b0), .B(mmu_1_led_r7[5]));
  Button button_5 (.out(button_1_out[3]));
  Button button_6 (.out(button_1_out[2]));
  DipSwitch dipswitch_9 (.out(dipswitch_1_out[3]));
  DipSwitch dipswitch_10 (.out(dipswitch_1_out[2]));
  DipSwitch dipswitch_11 (.out(dipswitch_3_out[3]));
  DipSwitch dipswitch_12 (.out(dipswitch_3_out[2]));
  Counter #(.Bits(8)) counter_1 (.en(1'b1), .C(not_3_out), .clr(decode_1_p1), .out(counter_1_out));  // open: ovf
  LightBulb lightbulb_25 (.A(1'b0), .B(mmu_1_led_r0[4]));
  LightBulb lightbulb_26 (.A(1'b0), .B(mmu_1_led_r0[3]));
  LightBulb lightbulb_27 (.A(1'b0), .B(mmu_1_led_r1[4]));
  LightBulb lightbulb_28 (.A(1'b0), .B(mmu_1_led_r1[3]));
  LightBulb lightbulb_29 (.A(1'b0), .B(mmu_1_led_r2[4]));
  LightBulb lightbulb_30 (.A(1'b0), .B(mmu_1_led_r2[3]));
  LightBulb lightbulb_31 (.A(1'b0), .B(mmu_1_led_r3[4]));
  LightBulb lightbulb_32 (.A(1'b0), .B(mmu_1_led_r3[3]));
  LightBulb lightbulb_33 (.A(1'b0), .B(mmu_1_led_r4[4]));
  LightBulb lightbulb_34 (.A(1'b0), .B(mmu_1_led_r4[3]));
  LightBulb lightbulb_35 (.A(1'b0), .B(mmu_1_led_r5[4]));
  LightBulb lightbulb_36 (.A(1'b0), .B(mmu_1_led_r5[3]));
  LightBulb lightbulb_37 (.A(1'b0), .B(mmu_1_led_r6[4]));
  LightBulb lightbulb_38 (.A(1'b0), .B(mmu_1_led_r6[3]));
  LightBulb lightbulb_39 (.A(1'b0), .B(mmu_1_led_r7[4]));
  LightBulb lightbulb_40 (.A(1'b0), .B(mmu_1_led_r7[3]));
  Button button_7 (.out(button_1_out[1]));
  Button UP (.out(button_1_out[0]));
  DipSwitch dipswitch_13 (.out(dipswitch_1_out[1]));
  DipSwitch dipswitch_14 (.out(dipswitch_1_out[0]));
  DipSwitch dipswitch_15 (.out(dipswitch_3_out[1]));
  DipSwitch dipswitch_16 (.out(dipswitch_3_out[0]));
  Telnet #(.telnetEscape("false"), .port(1234)) telnet_1 (
    .in({decode_1_p2_2, decode_1_p2}), .C(not_4_out), .wr(delay_1_out), .rd(delay_2_out),
    .out({decode_1_p2_2, decode_1_p2}), .av(telnet_1_av));
  LightBulb lightbulb_41 (.A(1'b0), .B(mmu_1_led_r0[2]));
  LightBulb lightbulb_42 (.A(1'b0), .B(mmu_1_led_r0[1]));
  LightBulb lightbulb_43 (.A(1'b0), .B(mmu_1_led_r1[2]));
  LightBulb lightbulb_44 (.A(1'b0), .B(mmu_1_led_r1[1]));
  LightBulb lightbulb_45 (.A(1'b0), .B(mmu_1_led_r2[2]));
  LightBulb lightbulb_46 (.A(1'b0), .B(mmu_1_led_r2[1]));
  LightBulb lightbulb_47 (.A(1'b0), .B(mmu_1_led_r3[2]));
  LightBulb lightbulb_48 (.A(1'b0), .B(mmu_1_led_r3[1]));
  LightBulb lightbulb_49 (.A(1'b0), .B(mmu_1_led_r4[2]));
  LightBulb lightbulb_50 (.A(1'b0), .B(mmu_1_led_r4[1]));
  LightBulb lightbulb_51 (.A(1'b0), .B(mmu_1_led_r5[2]));
  LightBulb lightbulb_52 (.A(1'b0), .B(mmu_1_led_r5[1]));
  LightBulb lightbulb_53 (.A(1'b0), .B(mmu_1_led_r6[2]));
  LightBulb lightbulb_54 (.A(1'b0), .B(mmu_1_led_r6[1]));
  LightBulb lightbulb_55 (.A(1'b0), .B(mmu_1_led_r7[2]));
  LightBulb lightbulb_56 (.A(1'b0), .B(mmu_1_led_r7[1]));
  // Probe on counter_1_out
  LightBulb lightbulb_57 (.A(1'b0), .B(mmu_1_led_r0[0]));
  LightBulb lightbulb_58 (.A(1'b0), .B(mmu_1_led_r1[0]));
  LightBulb lightbulb_59 (.A(1'b0), .B(mmu_1_led_r2[0]));
  LightBulb lightbulb_60 (.A(1'b0), .B(mmu_1_led_r3[0]));
  LightBulb lightbulb_61 (.A(1'b0), .B(mmu_1_led_r4[0]));
  LightBulb lightbulb_62 (.A(1'b0), .B(mmu_1_led_r5[0]));
  LightBulb lightbulb_63 (.A(1'b0), .B(mmu_1_led_r6[0]));
  LightBulb lightbulb_64 (.A(1'b0), .B(mmu_1_led_r7[0]));
  not not_5 (not_5_out, button_1_out[0]);
  Delay delay_3 (.in(not_5_out), .out(delay_3_out));
  and and_2 (and_2_out, button_1_out[0], delay_3_out);
  Counter #(.Bits(8)) counter_2 (.en(1'b1), .C(and_2_out), .clr(1'b0), .out(counter_2_out));  // open: ovf
  // Probe on counter_2_out

  // Notes on the sheet:
  //   clk: Hz: 2147483647
  //   SP
  //   ALU
  //   MAR
  //   PC_a
  //   PC_b
  //   A
  //   PCa
  //   PCb
  //   B
endmodule
