// Logisim project cpu5.circ as structural Verilog: 1 circuit, main circuit main
module main (
  input  in_1,
  input  in_2,
  input  in_3,
  input  in_4,
  input  in_5
);

  wire a_in, a_out, alu_d, alu_out, and_3_out, and_4_out, and_5_out, and_6_out, and_7_out, and_8_out,
       and_12_out, and_18_out, and_19_out, and_24_out, and_33_out, and_35_out, and_46_out, aop_in, b_in,
       b_out, bit_dbl, button_1_out, clock_1_out, cond_true, dec_s, decoder_1_out0, decoder_1_out1,
       decoder_1_out2, decoder_1_out3, decoder_1_out4, decoder_1_out5, decoder_1_out6, decoder_1_out7,
       decoder_2_out7, decoder_3_out0, decoder_4_out9, decoder_4_out10, decoder_4_out11, decoder_4_out12,
       decoder_4_out13, decoder_5_out0, decoder_5_out1, decoder_5_out2, decoder_5_out3, inc_s, inc_x, inc_x0,
       inc_x1, inc_y, inc_y0, inc_y1, ld_alu_cmd, ld_ir, ld_mh, ld_ml, ld_sh, ld_sl, ld_xh, ld_xl, ld_yh,
       ld_yl, lit_out, m_a, m_a0, m_a1, mem_in, mem_out, mh_in, ml_in, mr, mr0, mr3, mw, mw0, mw1, not_2_out,
       not_3_out, not_4_out, not_5_out, not_7_out, not_8_out, not_9_out, not_11_out, not_12_out, nsel_a_x,
       or_1_out, or_2_out, or_3_out, or_4_out, or_5_out, or_6_out, or_7_out, or_8_out, or_10_out, or_11_out,
       or_21_out, or_22_out, or_24_out, or_25_out, s_a, s_a1, sel_a_x, sel_in, sel_out, sel_ram, sh_in,
       SL_carry, sl_in, stk_in, stk_out, toggle0, toggle1, toggle_reg, toggle_reg_cond, undriven, word2, x_a,
       x_a0, x_a1, xh_d, XL_carry, xl_d, y_a, y_a0, y_a1, yh_d, YL_carry, yl_d;
  wire [0:0] IR_q;
  wire [1:0] YH_2_q;
  wire [2:0] and_17_out, sel_src;
  wire [3:0] B_XH_out, B_XH_out_2, sel_dst;
  wire [7:0] A_XL_out, button_9_out, controlled_buffer_8_out, controlled_buffer_11_out, d_bus, FLAGS_q, MH_q,
       ML_q, register_1_q, register_2_q, register_3_q, register_4_q, register_5_q, register_6_q,
       register_7_q, register_8_q, register_9_q, rom_1_data, rom_2_data, SH_q, SL_q, XH_q, XL_q, YH_q, YL_q;
  wire [15:0] a_bus;

  Hex_Digit_Display hex_digit_display_1 (.value(d_bus[3:0]));  // open: dp
  Hex_Digit_Display hex_digit_display_2 (.value(d_bus[7:4]));  // open: dp
  assign d_bus = xl_d ? XL_q : 8'bz;  // Controlled_Buffer controlled_buffer_1
  assign d_bus = xh_d ? XH_q : 8'bz;  // Controlled_Buffer controlled_buffer_2
  assign d_bus = yl_d ? YL_q : 8'bz;  // Controlled_Buffer controlled_buffer_3
  assign d_bus = yh_d ? YH_q : 8'bz;  // Controlled_Buffer controlled_buffer_4
  Register ML (.D(d_bus), .Q(ML_q), .clk(ld_ml));  // open: en, clr
  Register MH (.D(d_bus), .Q(MH_q), .clk(ld_mh));  // open: en, clr
  assign d_bus = in_3 ? SL_q : 8'bz;  // Controlled_Buffer controlled_buffer_5
  assign d_bus = in_4 ? SH_q : 8'bz;  // Controlled_Buffer controlled_buffer_6
  not not_1 (sel_ram, a_bus[15]);
  Counter XL (.load(ld_xl), .D(d_bus), .count(inc_x), .Q(XL_q), .carry(XL_carry), .clk(or_1_out), .clr(button_1_out));
  or or_1 (or_1_out, ld_xl, inc_x);
  Counter XH (.load(ld_xh), .D(d_bus), .count(XL_carry), .Q(XH_q), .clk(or_2_out), .clr(button_1_out));  // open: carry
  or or_2 (or_2_out, inc_x, ld_xh);
  Counter YL (.load(ld_yl), .D(d_bus), .count(inc_y), .Q(YL_q), .carry(YL_carry), .clk(or_3_out), .clr(button_1_out));
  or or_3 (or_3_out, ld_yl, inc_y);
  Counter YH (.load(ld_yh), .D(d_bus), .count(YL_carry), .Q(YH_q), .clk(or_4_out), .clr(button_1_out));  // open: carry
  or or_4 (or_4_out, inc_y, ld_yh);
  or or_5 (or_5_out, inc_s, dec_s);
  or or_6 (or_6_out, ld_sl, dec_s);
  or or_7 (or_7_out, ld_sl, or_5_out);
  or or_8 (or_8_out, or_5_out, ld_sh);
  Register IR (.D(d_bus), .Q({bit_dbl, sel_src, sel_dst[3:1], IR_q[0]}), .clk(ld_ir));  // open: en, clr
  not not_2 (not_2_out, a_bus[14]);
  and and_1 (sel_in, not_2_out, a_bus[15]);
  and and_2 (sel_out, a_bus[14], a_bus[15]);
  Hex_Digit_Display hex_digit_display_3 (.value(a_bus[15:12]));  // open: dp
  Button button_1 (.out(button_1_out));
  assign a_bus = m_a ? {MH_q, ML_q} : 16'bz;  // Controlled_Buffer MA
  Counter SL (.load(or_6_out), .D(d_bus), .count(or_5_out), .Q(SL_q), .carry(SL_carry), .clk(or_7_out));  // open: clr
  Counter SH (.load(ld_sh), .D(d_bus), .count(SL_carry), .Q(SH_q), .clk(or_8_out));  // open: carry, clr
  and and_3 (and_3_out, sel_ram, mr);
  and and_4 (and_4_out, sel_ram, mw);
  Hex_Digit_Display hex_digit_display_4 (.value(a_bus[7:4]));  // open: dp
  Hex_Digit_Display hex_digit_display_5 (.value(a_bus[11:8]));  // open: dp
  assign a_bus = x_a ? {XH_q, XL_q} : 16'bz;  // Controlled_Buffer XA
  assign a_bus = y_a ? {YH_q, YL_q} : 16'bz;  // Controlled_Buffer YA
  assign a_bus = s_a ? {SH_q, SL_q} : 16'bz;  // Controlled_Buffer SA
  assign d_bus = and_3_out ? controlled_buffer_8_out : 8'bz;  // Controlled_Buffer controlled_buffer_7
  assign controlled_buffer_8_out = and_4_out ? d_bus : 8'bz;  // Controlled_Buffer controlled_buffer_8
  not not_3 (not_3_out, and_4_out);
  and and_5 (and_5_out, sel_out, mw);
  Hex_Digit_Display hex_digit_display_6 (.value(a_bus[3:0]));  // open: dp
  Hex_Digit_Display hex_digit_display_7 (.value(SH_q[7:4]));  // open: dp
  or or_9 (sel_dst[0], word2, IR_q[0]);
  Decoder #(.select(3)) decoder_1 (
    .out0(decoder_1_out0), .out1(decoder_1_out1), .out2(decoder_1_out2), .out3(decoder_1_out3),
    .out4(decoder_1_out4), .out5(decoder_1_out5), .out6(decoder_1_out6), .out7(decoder_1_out7),
    .sel(a_bus[2:0]), .en(and_5_out));
  Pull_Resistor pull_resistor_1 (.node(decoder_1_out0));
  Pull_Resistor pull_resistor_2 (.node(decoder_1_out1));
  Pull_Resistor pull_resistor_3 (.node(decoder_1_out3));
  Pull_Resistor pull_resistor_4 (.node(decoder_1_out2));
  assign A_XL_out = sel_a_x ? XL_q : 8'bz;  // Controlled_Buffer A_XL
  assign A_XL_out = not_4_out ? YL_q : 8'bz;  // Controlled_Buffer A_YL
  not not_4 (not_4_out, sel_a_x);
  assign {B_XH_out_2, B_XH_out} = sel_a_x ? XH_q : 8'bz;  // Controlled_Buffer B_XH
  assign {B_XH_out_2, B_XH_out} = not_5_out ? YH_q : 8'bz;  // Controlled_Buffer B_YH
  not not_5 (not_5_out, sel_a_x);
  Hex_Digit_Display hex_digit_display_8 (.value(SH_q[3:0]));  // open: dp
  Pull_Resistor pull_resistor_5 (.node(decoder_1_out5));
  Pull_Resistor pull_resistor_6 (.node(decoder_1_out6));
  Pull_Resistor pull_resistor_7 (.node(decoder_1_out7));
  Pull_Resistor pull_resistor_8 (.node(decoder_1_out4));
  Register register_1 (.D(d_bus), .Q(register_1_q), .clk(ld_alu_cmd));  // open: en, clr
  RAM #(.addrWidth(15), .bus("asynch")) ram_1 (
    .addr(a_bus[14:0]), .data(controlled_buffer_8_out), .ld(not_3_out));  // open: sel, clr
  Register register_2 (.D(d_bus), .Q(register_2_q), .clk(decoder_1_out0));  // open: en, clr
  Register register_3 (.D(d_bus), .Q(register_3_q), .clk(decoder_1_out2));  // open: en, clr
  Register register_4 (.D(d_bus), .Q(register_4_q), .clk(decoder_1_out4));  // open: en, clr
  Register register_5 (.D(d_bus), .Q(register_5_q), .clk(decoder_1_out6));  // open: en, clr
  Hex_Digit_Display hex_digit_display_9 (.value(A_XL_out[7:4]));  // open: dp
  Hex_Digit_Display hex_digit_display_10 (.value(A_XL_out[3:0]));  // open: dp
  or or_10 (or_10_out, mr0, m_a0);
  or or_11 (or_11_out, inc_s, mr3);
  or or_12 (x_a, x_a0, x_a1);
  or or_13 (y_a, y_a0, y_a1);
  or or_14 (m_a, m_a0, m_a1);
  or or_15 (s_a, inc_s, s_a1);
  or or_16 (mw, mw0, mw1);
  Decoder #(.select(3)) decoder_2 (
    .out0(a_out), .out1(b_out), .out2(alu_out), .out3(mem_out), .out4(stk_out), .out5(lit_out),
    .out7(decoder_2_out7), .sel(sel_src));  // open: out6, en
  Hex_Digit_Display hex_digit_display_11 (.value(B_XH_out_2));  // open: dp
  or or_17 (mr, or_10_out, or_11_out);
  Register register_6 (.D(d_bus), .Q(register_6_q), .clk(decoder_1_out1));  // open: en, clr
  DotMatrix #(.inputtype("row"), .matrixcols(8), .matrixrows(8), .dotshape("circle")) dotmatrix_1 (
    .row0(register_2_q), .row1(register_6_q), .row2(register_3_q), .row3(register_7_q), .row4(register_4_q),
    .row5(register_8_q), .row6(register_5_q), .row7(register_9_q));
  Register register_7 (.D(d_bus), .Q(register_7_q), .clk(decoder_1_out3));  // open: en, clr
  Register register_8 (.D(d_bus), .Q(register_8_q), .clk(decoder_1_out5));  // open: en, clr
  Register register_9 (.D(d_bus), .Q(register_9_q), .clk(decoder_1_out7));  // open: en, clr
  ROM #(.addrWidth(13)) rom_1 (
    .addr({FLAGS_q[1], register_1_q[3:0], B_XH_out, A_XL_out[3:0]}), .data(rom_1_data));  // open: sel
  ROM #(.addrWidth(13)) rom_2 (
    .addr({rom_1_data[5], register_1_q[3:0], B_XH_out_2, A_XL_out[7:4]}), .data(rom_2_data));  // open: sel
  Hex_Digit_Display hex_digit_display_12 (.value(B_XH_out));  // open: dp
  Register FLAGS (
    .D({{5{1'b0}}, and_17_out[2], rom_2_data[5], and_17_out[0]}), .Q(FLAGS_q), .clk(alu_d));  // open: en, clr
  or or_18 (inc_x, inc_x0, inc_x1);
  or or_19 (inc_y, inc_y0, inc_y1);
  Hex_Digit_Display hex_digit_display_13 (.value(rom_2_data[3:0]));  // open: dp
  or or_20 (cond_true, or_21_out, and_18_out);
  and and_6 (and_6_out, or_24_out, a_out);
  and and_7 (and_7_out, mr, sel_in);
  Hex_Digit_Display hex_digit_display_14 (.value(rom_1_data[3:0]));  // open: dp
  assign d_bus = alu_d ? {rom_2_data[3:0], rom_1_data[3:0]} : 8'bz;  // Controlled_Buffer controlled_buffer_9
  or or_21 (or_21_out, and_12_out, and_19_out);
  and and_8 (and_8_out, or_24_out, b_out);
  and and_9 (alu_d, or_24_out, alu_out);
  and and_10 (xl_d, and_6_out, sel_a_x);
  and and_11 (yl_d, and_6_out, nsel_a_x);
  assign d_bus = and_7_out ? controlled_buffer_11_out : 8'bz;  // Controlled_Buffer controlled_buffer_10
  Decoder #(.select(3)) decoder_3 (
    .out0(decoder_3_out0), .sel(a_bus[2:0]), .en(undriven));  // open: out1, out2, out3, out4, out5, out6, out7
  and and_12 (and_12_out, register_1_q[4], FLAGS_q[0]);
  and and_13 (m_a0, or_24_out, mem_out);
  and and_14 (inc_s, or_24_out, stk_out);
  and and_15 (xh_d, and_8_out, sel_a_x);
  and and_16 (yh_d, and_8_out, nsel_a_x);
  Button button_2 (.out(button_9_out[7]));
  Button button_3 (.out(button_9_out[6]));
  Button button_4 (.out(button_9_out[5]));
  assign controlled_buffer_11_out = decoder_3_out0 ? button_9_out : 8'bz;  // Controlled_Buffer controlled_buffer_11
  and and_17 (and_17_out[0], rom_1_data[4], rom_2_data[4]);
  or or_22 (or_22_out, and_17_out[0], rom_2_data[5]);
  and and_18 (and_18_out, register_1_q[6], FLAGS_q[2]);
  and and_19 (and_19_out, register_1_q[5], FLAGS_q[1]);
  Decoder #(.select(4)) decoder_4 (
    .out0(a_in), .out1(b_in), .out2(ml_in), .out3(mh_in), .out4(sl_in), .out5(sh_in), .out6(mem_in),
    .out7(stk_in), .out8(aop_in), .out9(decoder_4_out9), .out10(decoder_4_out10), .out11(decoder_4_out11),
    .out12(decoder_4_out12), .out13(decoder_4_out13), .out14(toggle_reg_cond), .out15(toggle_reg),
    .sel(sel_dst));  // open: en
  and and_20 (mr3, or_24_out, lit_out);
  Button button_5 (.out(button_9_out[3]));
  Button button_6 (.out(button_9_out[2]));
  Button button_7 (.out(button_9_out[4]));
  Button button_8 (.out(button_9_out[1]));
  not not_6 (and_17_out[2], or_22_out);
  and and_21 (x_a1, mr3, nsel_a_x);
  and and_22 (y_a1, mr3, sel_a_x);
  Button button_9 (.out(button_9_out[0]));
  // AND_Gate and_23 has open pins: in0=decoder_5_out3, in1=stk_out, out=open
  Clock clock_1 (.out(clock_1_out));
  or or_23 (mr0, decoder_5_out0, decoder_5_out1);
  not not_7 (not_7_out, word2);
  and and_24 (and_24_out, decoder_5_out3, lit_out);
  Decoder #(.select(2)) decoder_5 (
    .out0(decoder_5_out0), .out1(decoder_5_out1), .out2(decoder_5_out2), .out3(decoder_5_out3), .sel(YH_2_q));  // open: en
  Counter #(.width(2), .max('h3)) YH_2 (
    .count(1'b1), .Q(YH_2_q), .clk(clock_1_out), .clr(button_1_out));  // open: load, D, carry
  and and_25 (ld_ir, not_7_out, decoder_5_out1);
  and and_26 (dec_s, decoder_5_out0, stk_in);
  and and_27 (inc_x1, and_24_out, not_8_out);
  not not_8 (not_8_out, sel_a_x);
  and and_28 (inc_y1, and_24_out, sel_a_x);
  or or_24 (or_24_out, decoder_5_out2, decoder_5_out3);
  not not_9 (not_9_out, decoder_5_out3);
  not not_10 (nsel_a_x, sel_a_x);
  not not_11 (not_11_out, sel_a_x);
  not not_12 (not_12_out, sel_a_x);
  and and_29 (x_a0, mr0, not_11_out);
  and and_30 (y_a0, mr0, sel_a_x);
  and and_31 (inc_x0, ld_ir, not_12_out);
  and and_32 (inc_y0, ld_ir, sel_a_x);
  and and_33 (and_33_out, decoder_5_out3, a_in);
  T_Flip_Flop t_ff_1 (.clk(not_9_out), .T(bit_dbl), .Q(word2));  // open: Qn, preset, reset, en
  and and_34 (ld_ml, decoder_5_out3, ml_in);
  and and_35 (and_35_out, decoder_5_out3, b_in);
  and and_36 (ld_xl, and_33_out, sel_a_x);
  and and_37 (ld_yl, and_33_out, nsel_a_x);
  and and_38 (ld_mh, decoder_5_out3, mh_in);
  and and_39 (ld_xh, and_35_out, sel_a_x);
  and and_40 (ld_yh, and_35_out, nsel_a_x);
  or or_25 (or_25_out, toggle0, toggle1);
  and and_41 (ld_sl, decoder_5_out3, sl_in);
  and and_42 (ld_sh, decoder_5_out3, sh_in);
  and and_43 (mw0, decoder_5_out3, mem_in);
  and and_44 (mw1, decoder_5_out3, stk_in);
  T_Flip_Flop t_ff_2 (.clk(or_25_out), .T(1'b1), .Q(sel_a_x));  // open: Qn, preset, reset, en
  and and_45 (ld_alu_cmd, decoder_5_out3, aop_in);
  and and_46 (and_46_out, decoder_5_out3, toggle_reg_cond);
  and and_47 (toggle0, decoder_5_out3, toggle_reg);
  // AND_Gate and_48 has open pins: in0=or_24_out, in1=a_in, out=open
  and and_49 (toggle1, and_46_out, cond_true);
  // AND_Gate and_50 has open pins: in0=or_24_out, in1=b_in, out=open
  // AND_Gate and_51 has open pins: in0=or_24_out, in1=ml_in, out=open
  // AND_Gate and_52 has open pins: in0=or_24_out, in1=mh_in, out=open
  // AND_Gate and_53 has open pins: in0=or_24_out, in1=sh_in, out=open
  // AND_Gate and_54 has open pins: in0=or_24_out, in1=sl_in, out=open
  and and_55 (m_a1, or_24_out, mem_in);
  // AND_Gate and_56 has open pins: in0=or_24_out, in1=aop_in, out=open
  and and_57 (s_a1, or_24_out, stk_in);
  // AND_Gate and_58 has open pins: in0=or_24_out, in1=toggle_reg, out=open

  // Other names for the same wires on the sheet: sel_io = a_bus[15]; mr1 = m_a0; mr2 = inc_s; s_a0 = inc_s;
  //   sh_d = in_4; sl_d = in_3

  // Notes on the sheet:
  //   ++++++++++++++++++++++++++++
  //   Data bus
  //   Address bus
  //   Carry in
  //   carry
  //   ALU High
  //   ALU Low
  //   contents of rom_1 (hex, n*v repeats v):
  //   10 1 2 3 4 5 6 7 8 9 a b c d e f 1 2 3 4 5 6 7 8 9 a b c d e f 30 2 3 4 5 6 7 8 9 a b c d e f 30 21
  //   3 4 5 6 7 8 9 a b c d e f 30 21 22 4 5 6 7 8 9 a b c d e f 30 21 22 23 5 6 7 8 9 a b c d e f 30 21
  //   22 23 24 6 7 8 9 a b c d e f 30 21 22 23 24 25 7 8 9 a b c d e f 30 21 22 23 24 25 26 8 9 a b c d e
  //   f 30 21 22 23 24 25 26 27 9 a b c d e f 30 21 22 23 24 25 26 27 28 a b c d e f 30 21 22 23 24 25 26
  //   27 28 29 b c d e f 30 21 22 23 24 25 26 27 28 29 2a c d e f 30 21 22 23 24 25 26 27 28 29 2a 2b d e
  //   f 30 21 22 23 24 25 26 27 28 29 2a 2b 2c e f 30 21 22 23 24 25 26 27 28 29 2a 2b 2c 2d f 30 21 22 23
  //   24 25 26 27 28 29 2a 2b 2c 2d 2e 10 1 2 3 4 5 6 7 8 9 a b c d e f 2f 10 1 2 3 4 5 6 7 8 9 a b c d e
  //   2e 2f 10 1 2 3 4 5 6 7 8 9 a b c d 2d 2e 2f 10 1 2 3 4 5 6 7 8 9 a b c 2c 2d 2e 2f 10 1 2 3 4 5 6 7
  //   8 9 a b 2b 2c 2d 2e 2f 10 1 2 3 4 5 6 7 8 9 a 2a 2b 2c 2d 2e 2f 10 1 2 3 4 5 6 7 8 9 29 2a 2b 2c 2d
  //   2e 2f 10 1 2 3 4 5 6 7 8 28 29 2a 2b 2c 2d 2e 2f 10 1 2 3 4 5 6 7 27 28 29 2a 2b 2c 2d 2e 2f 10 1 2
  //   3 4 5 6 26 27 28 29 2a 2b 2c 2d 2e 2f 10 1 2 3 4 5 25 26 27 28 29 2a 2b 2c 2d 2e 2f 10 1 2 3 4 24 25
  //   26 27 28 29 2a 2b 2c 2d 2e 2f 10 1 2 3 23 24 25 26 27 28 29 2a 2b 2c 2d 2e 2f 10 1 2 22 23 24 25 26
  //   27 28 29 2a 2b 2c 2d 2e 2f 10 1 21 22 23 24 25 26 27 28 29 2a 2b 2c 2d 2e 2f 10 10 2f 2e 2d 2c 2b 2a
  //   29 28 27 26 25 24 23 22 21 10 2f 2e 2d 2c 2b 2a 29 28 27 26 25 24 23 22 21 10 2f 2e 2d 2c 2b 2a 29
  //   28 27 26 25 24 23 22 21 10 2f 2e 2d 2c 2b 2a 29 28 27 26 25 24 23 22 21 10 2f 2e 2d 2c 2b 2a 29 28
  //   27 26 25 24 23 22 21 10 2f 2e 2d 2c 2b 2a 29 28 27 26 25 24 23 22 21 10 2f 2e 2d 2c 2b 2a 29 28 27
  //   26 25 24 23 22 21 10 2f 2e 2d 2c 2b 2a 29 28 27 26 25 24 23 22 21 10 2f 2e 2d 2c 2b 2a 29 28 27 26
  //   25 24 23 22 21 10 2f 2e 2d 2c 2b 2a 29 28 27 26 25 24 23 22 21 10 2f 2e 2d 2c 2b 2a 29 28 27 26 25
  //   24 23 22 21 10 2f 2e 2d 2c 2b 2a 29 28 27 26 25 24 23 22 21 10 2f 2e 2d 2c 2b 2a 29 28 27 26 25 24
  //   23 22 21 10 2f 2e 2d 2c 2b 2a 29 28 27 26 25 24 23 22 21 10 2f 2e 2d 2c 2b 2a 29 28 27 26 25 24 23
  //   22 21 10 2f 2e 2d 2c 2b 2a 29 28 27 26 25 24 23 22 21 10 2 4 6 8 a c e 30 22 24 26 28 2a 2c 2e 10 2
  //   4 6 8 a c e 30 22 24 26 28 2a 2c 2e 10 2 4 6 8 a c e 30 22 24 26 28 2a 2c 2e 10 2 4 6 8 a c e 30 22
  //   24 26 28 2a 2c 2e 10 2 4 6 8 a c e 30 22 24 26 28 2a 2c 2e 10 2 4 6 8 a c e 30 22 24 26 28 2a 2c 2e
  //   10 2 4 6 8 a c e 30 22 24 26 28 2a 2c 2e 10 2 4 6 8 a c e 30 22 24 26 28 2a 2c 2e 10 2 4 6 8 a c e
  //   30 22 24 26 28 2a 2c 2e 10 2 4 6 8 a c e 30 22 24 26 28 2a 2c 2e 10 2 4 6 8 a c e 30 22 24 26 28 2a
  //   2c 2e 10 2 4 6 8 a c e 30 22 24 26 28 2a 2c 2e 10 2 4 6 8 a c e 30 22 24 26 28 2a 2c 2e 10 2 4 6 8 a
  //   c e 30 22 24 26 28 2a 2c 2e 10 2 4 6 8 a c e 30 22 24 26 28 2a 2c 2e 10 2 4 6 8 a c e 30 22 24 26 28
  //   2a 2c 2e 256*10 1 2 3 4 5 6 7 8 9 a b c d e f 30 1 2 3 4 5 6 7 8 9 a b c d e f 30 1 2 3 4 5 6 7 8 9
  //   a b c d e f 30 1 2 3 4 5 6 7 8 9 a b c d e f 30 1 2 3 4 5 6 7 8 9 a b c d e f 30 1 2 3 4 5 6 7 8 9 a
  //   b c d e f 30 1 2 3 4 5 6 7 8 9 a b c d e f 30 1 2 3 4 5 6 7 8 9 a b c d e f 30 1 2 3 4 5 6 7 8 9 a b
  //   c d e f 30 1 2 3 4 5 6 7 8 9 a b c d e f 30 1 2 3 4 5 6 7 8 9 a b c d e f 30 1 2 3 4 5 6 7 8 9 a b c
  //   d e f 30 1 2 3 4 5 6 7 8 9 a b c d e f 30 1 2 3 4 5 6 7 8 9 a b c d e f 30 1 2 3 4 5 6 7 8 9 a b c d
  //   e f 30 1 2 3 4 5 6 7 8 9 a b c d e f 30 10 1 2 3 4 5 6 7 8 9 a b c d e f 1 2 3 4 5 6 7 8 9 a b c d e
  //   f 30 2 3 4 5 6 7 8 9 a b c d e f 30 21 3 4 5 6 7 8 9 a b c d e f 30 21 22 4 5 6 7 8 9 a b c d e f 30
  //   21 22 23 5 6 7 8 9 a b c d e f 30 21 22 23 24 6 7 8 9 a b c d e f 30 21 22 23 24 25 7 8 9 a b c d e
  //   f 30 21 22 23 24 25 26 8 9 a b c d e f 30 21 22 23 24 25 26 27 9 a b c d e f 30 21 22 23 24 25 26 27
  //   28 a b c d e f 30 21 22 23 24 25 26 27 28 29 b c d e f 30 21 22 23 24 25 26 27 28 29 2a c d e f 30
  //   21 22 23 24 25 26 27 28 29 2a 2b d e f 30 21 22 23 24 25 26 27 28 29 2a 2b 2c e f 30 21 22 23 24 25
  //   26 27 28 29 2a 2b 2c 2d f 30 21 22 23 24 25 26 27 28 29 2a 2b 2c 2d 2e 10 1 2 3 4 5 6 7 8 9 a b c d
  //   e f 2f 10 1 2 3 4 5 6 7 8 9 a b c d e 2e 2f 10 1 2 3 4 5 6 7 8 9 a b c d 2d 2e 2f 10 1 2 3 4 5 6 7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
  //   contents of rom_2 (hex, n*v repeats v):
  //   10 1 2 3 4 5 6 7 8 9 a b c d e f 1 2 3 4 5 6 7 8 9 a b c d e f 30 2 3 4 5 6 7 8 9 a b c d e f 30 21
  //   3 4 5 6 7 8 9 a b c d e f 30 21 22 4 5 6 7 8 9 a b c d e f 30 21 22 23 5 6 7 8 9 a b c d e f 30 21
  //   22 23 24 6 7 8 9 a b c d e f 30 21 22 23 24 25 7 8 9 a b c d e f 30 21 22 23 24 25 26 8 9 a b c d e
  //   f 30 21 22 23 24 25 26 27 9 a b c d e f 30 21 22 23 24 25 26 27 28 a b c d e f 30 21 22 23 24 25 26
  //   27 28 29 b c d e f 30 21 22 23 24 25 26 27 28 29 2a c d e f 30 21 22 23 24 25 26 27 28 29 2a 2b d e
  //   f 30 21 22 23 24 25 26 27 28 29 2a 2b 2c e f 30 21 22 23 24 25 26 27 28 29 2a 2b 2c 2d f 30 21 22 23
  //   24 25 26 27 28 29 2a 2b 2c 2d 2e 10 1 2 3 4 5 6 7 8 9 a b c d e f 2f 10 1 2 3 4 5 6 7 8 9 a b c d e
  //   2e 2f 10 1 2 3 4 5 6 7 8 9 a b c d 2d 2e 2f 10 1 2 3 4 5 6 7 8 9 a b c 2c 2d 2e 2f 10 1 2 3 4 5 6 7
  //   8 9 a b 2b 2c 2d 2e 2f 10 1 2 3 4 5 6 7 8 9 a 2a 2b 2c 2d 2e 2f 10 1 2 3 4 5 6 7 8 9 29 2a 2b 2c 2d
  //   2e 2f 10 1 2 3 4 5 6 7 8 28 29 2a 2b 2c 2d 2e 2f 10 1 2 3 4 5 6 7 27 28 29 2a 2b 2c 2d 2e 2f 10 1 2
  //   3 4 5 6 26 27 28 29 2a 2b 2c 2d 2e 2f 10 1 2 3 4 5 25 26 27 28 29 2a 2b 2c 2d 2e 2f 10 1 2 3 4 24 25
  //   26 27 28 29 2a 2b 2c 2d 2e 2f 10 1 2 3 23 24 25 26 27 28 29 2a 2b 2c 2d 2e 2f 10 1 2 22 23 24 25 26
  //   27 28 29 2a 2b 2c 2d 2e 2f 10 1 21 22 23 24 25 26 27 28 29 2a 2b 2c 2d 2e 2f 10 10 2f 2e 2d 2c 2b 2a
  //   29 28 27 26 25 24 23 22 21 10 2f 2e 2d 2c 2b 2a 29 28 27 26 25 24 23 22 21 10 2f 2e 2d 2c 2b 2a 29
  //   28 27 26 25 24 23 22 21 10 2f 2e 2d 2c 2b 2a 29 28 27 26 25 24 23 22 21 10 2f 2e 2d 2c 2b 2a 29 28
  //   27 26 25 24 23 22 21 10 2f 2e 2d 2c 2b 2a 29 28 27 26 25 24 23 22 21 10 2f 2e 2d 2c 2b 2a 29 28 27
  //   26 25 24 23 22 21 10 2f 2e 2d 2c 2b 2a 29 28 27 26 25 24 23 22 21 10 2f 2e 2d 2c 2b 2a 29 28 27 26
  //   25 24 23 22 21 10 2f 2e 2d 2c 2b 2a 29 28 27 26 25 24 23 22 21 10 2f 2e 2d 2c 2b 2a 29 28 27 26 25
  //   24 23 22 21 10 2f 2e 2d 2c 2b 2a 29 28 27 26 25 24 23 22 21 10 2f 2e 2d 2c 2b 2a 29 28 27 26 25 24
  //   23 22 21 10 2f 2e 2d 2c 2b 2a 29 28 27 26 25 24 23 22 21 10 2f 2e 2d 2c 2b 2a 29 28 27 26 25 24 23
  //   22 21 10 2f 2e 2d 2c 2b 2a 29 28 27 26 25 24 23 22 21 10 2 4 6 8 a c e 30 22 24 26 28 2a 2c 2e 10 2
  //   4 6 8 a c e 30 22 24 26 28 2a 2c 2e 10 2 4 6 8 a c e 30 22 24 26 28 2a 2c 2e 10 2 4 6 8 a c e 30 22
  //   24 26 28 2a 2c 2e 10 2 4 6 8 a c e 30 22 24 26 28 2a 2c 2e 10 2 4 6 8 a c e 30 22 24 26 28 2a 2c 2e
  //   10 2 4 6 8 a c e 30 22 24 26 28 2a 2c 2e 10 2 4 6 8 a c e 30 22 24 26 28 2a 2c 2e 10 2 4 6 8 a c e
  //   30 22 24 26 28 2a 2c 2e 10 2 4 6 8 a c e 30 22 24 26 28 2a 2c 2e 10 2 4 6 8 a c e 30 22 24 26 28 2a
  //   2c 2e 10 2 4 6 8 a c e 30 22 24 26 28 2a 2c 2e 10 2 4 6 8 a c e 30 22 24 26 28 2a 2c 2e 10 2 4 6 8 a
  //   c e 30 22 24 26 28 2a 2c 2e 10 2 4 6 8 a c e 30 22 24 26 28 2a 2c 2e 10 2 4 6 8 a c e 30 22 24 26 28
  //   2a 2c 2e 257*10 1 2 3 4 5 6 7 8 9 a b c d e f 10 1 2 3 4 5 6 7 8 9 a b c d e f 10 1 2 3 4 5 6 7 8 9
  //   a b c d e f 10 1 2 3 4 5 6 7 8 9 a b c d e f 10 1 2 3 4 5 6 7 8 9 a b c d e f 10 1 2 3 4 5 6 7 8 9 a
  //   b c d e f 10 1 2 3 4 5 6 7 8 9 a b c d e f 10 1 2 3 4 5 6 7 8 9 a b c d e f 10 1 2 3 4 5 6 7 8 9 a b
  //   c d e f 10 1 2 3 4 5 6 7 8 9 a b c d e f 10 1 2 3 4 5 6 7 8 9 a b c d e f 10 1 2 3 4 5 6 7 8 9 a b c
  //   d e f 10 1 2 3 4 5 6 7 8 9 a b c d e f 10 1 2 3 4 5 6 7 8 9 a b c d e f 10 1 2 3 4 5 6 7 8 9 a b c d
  //   e f 10 1 2 3 4 5 6 7 8 9 a b c d e f 10 1 2 3 4 5 6 7 8 9 a b c d e f 1 2 3 4 5 6 7 8 9 a b c d e f
  //   30 2 3 4 5 6 7 8 9 a b c d e f 30 21 3 4 5 6 7 8 9 a b c d e f 30 21 22 4 5 6 7 8 9 a b c d e f 30
  //   21 22 23 5 6 7 8 9 a b c d e f 30 21 22 23 24 6 7 8 9 a b c d e f 30 21 22 23 24 25 7 8 9 a b c d e
  //   f 30 21 22 23 24 25 26 8 9 a b c d e f 30 21 22 23 24 25 26 27 9 a b c d e f 30 21 22 23 24 25 26 27
  //   28 a b c d e f 30 21 22 23 24 25 26 27 28 29 b c d e f 30 21 22 23 24 25 26 27 28 29 2a c d e f 30
  //   21 22 23 24 25 26 27 28 29 2a 2b d e f 30 21 22 23 24 25 26 27 28 29 2a 2b 2c e f 30 21 22 23 24 25
  //   26 27 28 29 2a 2b 2c 2d f 30 21 22 23 24 25 26 27 28 29 2a 2b 2c 2d 2e 10 1 2 3 4 5 6 7 8 9 a b c d
  //   e f 2f 10 1 2 3 4 5 6 7 8 9 a b c d e 2e 2f 10 1 2 3 4 5 6 7 8 9 a b c d 2d 2e 2f 10 1 2 3 4 5 6 7 8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
  //   carry_out
  //   zero_low
  //   zero_high
  //   =
  //   <
  //   >
  //   Deferred SP decrement to p0
endmodule
